# Fritzing sketch arduino-wiring (saved by Fritzing 0.9.3b)
breadboards: 1

parts:
  Part1 = Arduino BT
  NEOPIXEL1 = Neopixel Strip -- White (60/m)
  Part2 = Real Time Clock Module - DS1307 RTC Breakout Board
  DS1 = DS18B20 1-Wire Temperature Sensor [part_number=DS18B20]
  R1 = Photocell (LDR) [package=THT]
  R2 = Resistor [tolerance=±5% resistance=10k package="0603 [SMD]"]
  R3 = Resistor [tolerance=±5% resistance=10k package="0603 [SMD]"]

nets:
  N1: Part1.A4/SDA, Part2.SCL
  N2: Part1.A5/SCL, Part2.SDA
  N3: Part1.A0, DS1.DQ, R2.Pin_1
  N4: Part1.PWM_D5, NEOPIXEL1.+5V
  N5: Part1.RESET_WT11/D7, R1.pin_0, R3.Pin_1
  GND: Part1.GND, NEOPIXEL1.GND, Part2.GND, DS1.GND, R3.Pin_0
  5V: Part1.5V, NEOPIXEL1.DI, Part2.5V, DS1.VDD, R1.pin_1, R2.Pin_0

custom parts:
  Neopixel Strip -- White (60/m): Neopixel Strip, White, 60 pixels per meter.
